# Fritzing sketch Button-Test (saved by Fritzing 0.8.7b)
breadboards: 1

parts:
  Raspberry_Pi_B_rev1 = Raspberry Pi B rev2
  LED1 = LED - 5mm [color="Red (633nm)" package="5 mm [THT]"]
  S1 = Pushbutton [package="[THT]"]
  R1 = Resistor [tolerance=±5% resistance=1k package=THT]
  R2 = Resistor [tolerance=±5% resistance=470 package=THT]

nets:
  N1: Raspberry_Pi_B_rev1.3V3, S1.Pin_1, S1.Pin_2
  N2: Raspberry_Pi_B_rev1.GND, LED1.cathode
  N3: Raspberry_Pi_B_rev1.GPIO_27, R1.Pin_0
  N4: Raspberry_Pi_B_rev1.GPIO_4, R2.Pin_0
  N5: LED1.anode, R2.Pin_1
  N6: S1.Pin_3, S1.Pin_4, R1.Pin_1
