# Fritzing sketch button (saved by Fritzing 0.9.2b)
circuit board: 8.46667cm x 5.64444cm
breadboards: 1

parts:
  Bauteil1 = Arduino Uno (Rev3) - ICSP
  R2 = Resistor [tolerance=±5% resistance=10k package=THT]
  S2 = Pushbutton [package=THT]

nets:
  N1: Bauteil1.5V, S2.leg0
  N2: Bauteil1.GND, R2.Pin_0
  N3: Bauteil1.D7, R2.Pin_1, S2.leg1
