# Fritzing sketch button_led (saved by Fritzing 0.9.2b)
circuit board: 8.46667cm x 5.64444cm
breadboards: 1

parts:
  Bauteil1 = Arduino Uno (Rev3) - ICSP
  LED1 = LED - 3mm [color="Red (633nm)" package="3 mm [THT]"]
  R1 = Resistor [tolerance=±5% resistance=220 package=THT]
  R2 = Resistor [tolerance=±5% resistance=220 package=THT]
  S2 = Pushbutton [package=THT]

nets:
  N1: Bauteil1.5V, S2.leg0
  N2: Bauteil1.GND, LED1.cathode, R2.Pin_0
  N3: Bauteil1.D13/SCK, R1.Pin_0
  N4: Bauteil1.D7, R2.Pin_1, S2.leg1
  N5: LED1.anode, R1.Pin_1
