# Fritzing sketch buzzer_pot_button (saved by Fritzing 0.9.2b)
circuit board: 8.46667cm x 5.64444cm
breadboards: 1

parts:
  M1 = Arduino Uno (Rev3) - ICSP
  U1 = POT [package=pot_alpha_rv16af-20]
  J1 = Piezo Speaker
  R1 = Resistor [tolerance=±5% resistance=10k package=THT]
  S1 = Pushbutton [package=THT]

nets (from the schematic view):
  N1: M1.A2, U1.S
  N2: M1.5V, U1.E, R1.Pin_0, S1.leg0
  N3: M1.D9_PWM, J1.pin2
  N4: M1.GND, U1.A, J1.pin1
  N5: M1.D7, R1.Pin_1, S1.leg1
