# Fritzing sketch ldr_led (saved by Fritzing 0.9.2b)
breadboards: 1

parts:
  M1 = Arduino Uno (Rev3) - ICSP
  R2 = Resistor [tolerance=±5% resistance=1k package=THT]
  R1 = Photocell (LDR) [package=THT]
  LED1 = LED - 5mm [color="Red (633nm)" package="5 mm [THT]"]
  R3 = Resistor [tolerance=±5% resistance=220 package=THT]

nets:
  N1: M1.A0, R2.Pin_0, R1.pin_1
  N2: M1.5V, R1.pin_0
  N3: M1.D13/SCK, R3.Pin_1
  N4: M1.GND, R2.Pin_1, LED1.anode
  N5: LED1.cathode, R3.Pin_0
