# Fritzing sketch led_blink (saved by Fritzing 0.9.2b)
circuit board: 8.46667cm x 5.64444cm
breadboards: 1

parts:
  part = Arduino Uno (Rev3) - ICSP
  LED1 = LED - 3mm [color="Red (633nm)" package="3 mm [THT]"]
  R1 = Resistor [tolerance=±5% resistance=220 package=THT]

nets:
  N1: part.GND, LED1.cathode
  N2: part.D13/SCK, R1.Pin_0
  N3: LED1.anode, R1.Pin_1

// code stored in the sketch: led_blink.ino
int pinLED = 13;

void setup() {
  pinMode(pinLED, OUTPUT);
}

void loop() {
  digitalWrite(pinLED, HIGH);
  delay(1000);

  digitalWrite(pinLED, LOW);
  delay(1000);
}
