# Fritzing sketch poti_led (saved by Fritzing 0.9.2b)
circuit board: 8.46667cm x 5.64444cm
breadboards: 1

parts:
  M1 = Arduino Uno (Rev3) - ICSP
  U1 = POT [package=pot_alpha_rv16af-20]
  LED1 = LED - 5mm [color="Red (633nm)" package="5 mm [THT]"]
  R1 = Resistor [tolerance=±5% resistance=220 package=THT]

nets:
  N1: M1.A2, U1.S
  N2: M1.5V, U1.E
  N3: M1.GND, U1.A, LED1.anode
  N4: M1.D13/SCK, R1.Pin_1
  N5: LED1.cathode, R1.Pin_0
