# Fritzing sketch charlieplexing (saved by Fritzing 0.8.7b)
circuit board: 8.46667cm x 5.64444cm
breadboards: 1

parts:
  Raspberry_Pi_B_rev1 = Raspberry Pi B rev2
  LED4 = LED - 5mm [color="Red (633nm)" package="5 mm [THT]"]
  LED3 = LED - 5mm [color="Red (633nm)" package="5 mm [THT]"]
  LED2 = LED - 5mm [color="Red (633nm)" package="5 mm [THT]"]
  LED5 = LED - 5mm [color="Red (633nm)" package="5 mm [THT]"]
  LED6 = LED - 5mm [color="Red (633nm)" package="5 mm [THT]"]
  R1 = Resistor [tolerance=±5% resistance=470 package=THT]
  R2 = Resistor [tolerance=±5% resistance=470 package=THT]
  R3 = Resistor [tolerance=±5% resistance=470 package=THT]
  LED1 = LED - 5mm [color="Red (633nm)" package="5 mm [THT]"]

nets:
  N1: Raspberry_Pi_B_rev1.GPIO_23, R2.Pin_0
  N2: Raspberry_Pi_B_rev1.GPIO_18, R1.Pin_0
  N3: Raspberry_Pi_B_rev1.GPIO_24, R3.Pin_0
  N4: LED4.cathode, LED2.anode, LED5.anode, R2.Pin_1, LED1.cathode
  N5: LED4.anode, LED3.anode, LED5.cathode, LED6.cathode, R3.Pin_1
  N6: LED3.cathode, LED2.cathode, LED6.anode, R1.Pin_1, LED1.anode
