# Fritzing sketch motor-tester (saved by Fritzing 0.9.2b)
breadboards: 1

parts:
  S1 = H-Bridge with L298N
  Raspberry_Pi1 = Raspberry Pi 2
  M1 = DC Motor
  M2 = DC Motor
  VCC1 = 4 x AAA Battery Mount

nets:
  N1: S1.12V, VCC1.+
  GND: S1.GND, S1.IN1, S1.IN3, Raspberry_Pi1.GND, VCC1.-
  N2: S1.IN2, S1.IN4, Raspberry_Pi1.3v3
  N3: S1.M1-01, M1.pin_2
  N4: S1.M1-02, M1.pin_1
  N5: S1.M2-01, M2.pin_2
  N6: S1.M2-02, M2.pin_1

notes:
  6 V
  3.3 V
  TEST:
  Cambiar los cables de positivo a negativo
  LOW - LOW => OFF
  HIGH - HIGH => OFF
  LOW - HIGH => FWD
  HIGH - LOW => REV

custom parts:
  H-Bridge with L298N: h-bridge
