# Fritzing sketch photo-resistor (saved by Fritzing 0.8.7b)
circuit board: 8.46667cm x 5.64444cm
breadboards: 1

parts:
  Raspberry_Pi_B_rev1 = Raspberry Pi B rev2
  R1 = Photocell (LDR) [package=THT]
  C1 = Ceramic Capacitor [capacitance=1µF package="100 mil [THT, multilayer]"]
  LED1 = LED - 5mm [color="Red (633nm)" package="5 mm [THT]"]
  R2 = Resistor [tolerance=±5% resistance=470 package=THT]

nets:
  N1: Raspberry_Pi_B_rev1.3V3, R1.pin_0
  N2: Raspberry_Pi_B_rev1.GND, C1.1, LED1.anode
  N3: Raspberry_Pi_B_rev1.GPIO_23, R2.Pin_0
  N4: Raspberry_Pi_B_rev1.GPIO_18, R1.pin_1, C1.0
  N5: LED1.cathode, R2.Pin_1
