# Fritzing sketch motors-leds (saved by Fritzing 0.9.2b)
breadboards: 1

parts:
  S1 = H-Bridge with L298N
  Raspberry_Pi1 = Raspberry Pi 2
  M1 = DC Motor
  M2 = DC Motor
  VCC1 = 4 x AAA Battery Mount
  LED1 = smd LED [color="Green (565nm)" package="0805 [SMD]"]
  LED2 = smd LED [color="Green (565nm)" package="0805 [SMD]"]
  LED3 = smd LED [color="Red (633nm)" package="0805 [SMD]"]
  LED4 = smd LED [color="Red (633nm)" package="0805 [SMD]"]
  R1 = Resistor [tolerance=±5% resistance=220 package="0603 [SMD]"]
  R2 = Resistor [tolerance=±5% resistance=220 package="0603 [SMD]"]

nets:
  N1: S1.12V, VCC1.+
  GND: S1.GND, Raspberry_Pi1.GND, VCC1.-
  N2: S1.IN1, Raspberry_Pi1.GPIO17, LED2.cathode, LED4.anode
  N3: S1.IN2, Raspberry_Pi1.GPIO27, R2.Pin_0
  N4: S1.IN3, Raspberry_Pi1.GPIO22, LED1.cathode, LED3.anode
  N5: S1.IN4, Raspberry_Pi1.GPIO23, R1.Pin_0
  N6: S1.M1-01, M1.pin_2
  N7: S1.M1-02, M1.pin_1
  N8: S1.M2-01, M2.pin_2
  N9: S1.M2-02, M2.pin_1
  N10: LED1.anode, LED3.cathode, R1.Pin_1
  N11: LED2.anode, LED4.cathode, R2.Pin_1

notes:
  6 V
  3.3 V

custom parts:
  H-Bridge with L298N: h-bridge
