# Fritzing sketch motors (saved by Fritzing 0.9.2b)
breadboards: 1

parts:
  S1 = H-Bridge with L298N
  Raspberry_Pi1 = Raspberry Pi 2
  M1 = DC Motor
  M2 = DC Motor
  VCC1 = 4 x AAA Battery Mount

nets:
  N1: S1.12V, VCC1.+
  GND: S1.GND, Raspberry_Pi1.GND, VCC1.-
  N2: S1.IN1, Raspberry_Pi1.GPIO17
  N3: S1.IN2, Raspberry_Pi1.GPIO27
  N4: S1.IN3, Raspberry_Pi1.GPIO22
  N5: S1.IN4, Raspberry_Pi1.GPIO23
  N6: S1.M1-01, M1.pin_2
  N7: S1.M1-02, M1.pin_1
  N8: S1.M2-01, M2.pin_2
  N9: S1.M2-02, M2.pin_1

notes:
  6 V
  3.3 V

custom parts:
  H-Bridge with L298N: h-bridge
