# Fritzing sketch speaker (saved by Fritzing 0.8.7b)

parts:
  Raspberry_Pi_B_rev1 = Raspberry Pi B rev2
  SPKR1 = Loudspeaker

nets:
  N1: Raspberry_Pi_B_rev1.GND, SPKR1.pin1
  N2: Raspberry_Pi_B_rev1.GPIO_18, SPKR1.pin2
